# Fritzing sketch RelayBoard (saved by Fritzing 0.8.7b)
circuit board: 5.52611cm x 5.19726cm
breadboards: 1

parts:
  J1 = female pin header, 3 pins [form="♀ (female)"]
  K1 = Relay [part_number=FRS1B-S package=THT]
  RL = Resistor [tolerance=±5% resistance=220 package=THT]
  RR = Resistor [tolerance=±5% resistance=220 package=THT]
  D1 = Rectifier Diode [part_number=1N4001 package="300 mil [THT]"]
  LED4 = LED - 5mm [color="Red (633nm)" package="5 mm [THT]"]
  Q3 = NPN-Transistor [package="TO92 [THT]"]
  RT1 = Resistor [tolerance=±5% resistance=1k package=THT]
  J2 = female pin header, 3 pins [form="♀ (female)"]

nets:
  N1: J1.pin1, RL.Pin_1, RR.Pin_1
  N2: J1.pin2, LED4.anode, RT1.Pin_1
  N3: J1.pin3, Q3.C
  N4: K1.A, J2.pin3
  N5: K1.COIL1, RR.Pin_0, D1.anode
  N6: K1.C1, K1.C2, J2.pin2
  N7: K1.COIL2, D1.cathode, Q3.E
  N8: K1.B, J2.pin1
  N9: RL.Pin_0, LED4.cathode
  N10: Q3.B, RT1.Pin_0

notes:
  1. GND
  2. IN: changes relay state
  3. VCC, 5V
  Output
  Either 1-2 are connected or 2-3 are connected
